# Fritzing sketch Proj01-basic (saved by Fritzing 0.7.4b)
breadboards: 2

parts:
  U1 = Arduino Mega
  Part1 = Arduino Wireless SD Shield  # not connected
  R1 = Rotary Potentiometer (Small) [maximum_resistance=100kΩ]  # not connected
  R2 = Resistor [tolerance=±5% resistance=220 package=THT]  # not connected
  LED1 = LED - 5mm [color="Red (633nm)" package="5 mm [THT]"]  # not connected
  GLCD_128x1 = LCD screen
  U2 = XBee  # not connected
  R3 = Trimmer Potentiometer [maximum_resistance=10kΩ package=THT]  # not connected
  R4 = Photocell (LDR) [package=THT]
  R5 = Resistor [tolerance=±5% resistance=220 package=THT]
  T1 = LM35 Temperature Sensor [package="TO92 [THT]"]

nets:
  +5V: U1.+5V, GLCD_128x1.VDD, R4.pin_0, T1.+Vs
  GND: U1.GND, GLCD_128x1.VSS, GLCD_128x1.R/W, GLCD_128x1.LED-, R5.Pin_0, T1.GND
  N1: U1.A0, T1.Vout
  N2: U1.A1, R4.pin_1, R5.Pin_1
  N3: U1.D42, GLCD_128x1.LED+
  N4: U1.D43, GLCD_128x1.V0
  N5: U1.D44, GLCD_128x1.DB4
  N6: U1.D45, GLCD_128x1.DB5
  N7: U1.D46, GLCD_128x1.DB6
  N8: U1.D47, GLCD_128x1.DB7
  N9: U1.D48, GLCD_128x1.E
  N10: U1.D49, GLCD_128x1.RS
